# Fritzing sketch Pylon (saved by Fritzing 0.9.3b)
circuit board: 3.73207cm x 6.02299cm
breadboards: 1

parts:
  Arduino = Arduino Nano (Rev3.0)
  R2 = Resistor [tolerance=±5% resistance=220 package=THT]
  R3 = Resistor [tolerance=±5% resistance=220 package=THT]
  LED = RGB LED (com. cathode, rgb) [package="5 mm [THT]"]
  R1 = Resistor [tolerance=±5% resistance=220 package=THT]
  MPU = InvenSense MPU6050
  HC12 = Header 6 [package=molex-1x6-ra]

nets:
  GND: Arduino.GND, LED.common_cathode, MPU.GND, HC12.2
  N1: Arduino.D2, HC12.4
  N2: Arduino.D3, HC12.3
  N3: Arduino.D4, R1.Pin_0
  N4: Arduino.D5, R2.Pin_0
  N5: Arduino.D6, R3.Pin_0
  5V: Arduino.5V, MPU.VCC, HC12.1
  N6: Arduino.A5, MPU.SCL
  N7: Arduino.A4, MPU.SDA
  N8: R2.Pin_1, LED.green_anode
  N9: R3.Pin_1, LED.blue_anode
  N10: LED.red_anode, R1.Pin_1
