# Fritzing sketch Receiver (saved by Fritzing 0.9.3b)
circuit board: 3.73207cm x 6.02299cm
breadboards: 1

parts:
  Arduino = Arduino Nano (Rev3.0)
  HM10 = Header 6 [package=molex-1x6-ra]
  HC12 = Header 6 [package=molex-1x6-ra]
  R2 = Resistor [tolerance=±5% resistance=220 package=THT]
  R3 = Resistor [tolerance=±5% resistance=220 package=THT]
  Pieper = Piezo Speaker
  LED = RGB LED (com. cathode, rgb) [package="5 mm [THT]"]
  Button = Momentary Switch [package=ksa_sealed_tac_switch]
  R1 = Resistor [tolerance=±5% resistance=220 package=THT]

nets:
  N1: Arduino.D1/TX, HM10.5
  N2: Arduino.D0/RX, HM10.4
  N3: Arduino.GND, HM10.3, HC12.4, Pieper.pin2, LED.common_cathode, Button.2
  N4: Arduino.D3, Button.4
  N5: Arduino.D6, HC12.3
  N6: Arduino.D7, HC12.2
  N7: Arduino.D8, R1.Pin_1
  N8: Arduino.D9, R2.Pin_1
  N9: Arduino.D10, R3.Pin_1
  N10: Arduino.D11/MOSI, Pieper.pin1
  N11: Arduino.5V, HM10.2, HC12.5
  N12: R2.Pin_0, LED.green_anode
  N13: R3.Pin_0, LED.blue_anode
  N14: LED.red_anode, R1.Pin_0
